# Fritzing sketch bluetooth (saved by Fritzing 0.9.3b)

parts:
  Part1 = Arduino Mega ADK (Rev3)
  Part2 = Bluetooth HC-05 Macho
  R2 = Resistor [tolerance=±5% resistance=100 package=THT]
  R3 = Resistor [tolerance=±5% resistance=200 package=THT]

nets:
  N1: Part1.D15/RX3, Part2.TXD
  N2: Part1.D14/TX3, R2.Pin_1
  N3: Part1.D9_PWM, Part2.Key
  5V: Part1.5V, Part2.VCC
  GND: Part1.GND, Part2.GND, R3.Pin_1
  N4: Part2.RXD, R2.Pin_0, R3.Pin_0
